# Fritzing sketch SmartParking.Wiring (saved by Fritzing 0.9.3b)
breadboards: 2

parts:
  Raspberry_Pi = Raspberry Pi B+
  Part1 = Arduino Uno (Rev3) - ICSP
  R1 = Resistor [tolerance=±5% resistance=220 package=THT]  # not connected
  LED1 = LED - 5mm [color="Red (633nm)" package="5 mm [THT]"]
  IR_Sensor = fc-51 [package=THT]
  Parking_1_-_Servo = Basic Servo
  Parking_2_-_Servo = Basic Servo
  LED4 = LED - 3mm [color="Red (633nm)" package="3 mm [THT]"]  # not connected
  LED5 = LED - 3mm [color="Red (633nm)" package="3 mm [THT]"]  # not connected
  R2 = Resistor [tolerance=±5% resistance=220 package=THT]
  R3 = Resistor [tolerance=±5% resistance=220 package=THT]
  LED6 = LED - 3mm [color="Red (633nm)" package="3 mm [THT]"]  # not connected
  LED7 = LED - 3mm [color="Red (633nm)" package="3 mm [THT]"]  # not connected
  R4 = Resistor [tolerance=±5% resistance=220 package=THT]
  R5 = Resistor [tolerance=±5% resistance=220 package=THT]

nets:
  N1: Raspberry_Pi.GPIO17, LED1.cathode
  N2: Raspberry_Pi.GPIO27, IR_Sensor.pin1
  N3: Raspberry_Pi.GND, LED1.anode, IR_Sensor.pin2
  N4: Raspberry_Pi.5V, IR_Sensor.pin3
  N5: Part1.ICSP_MOSI, Part1.D11_PWM/MOSI, Parking_1_-_Servo.pulse
  N6: Part1.D9_PWM, R2.Pin_0
  N7: Part1.D10_PWM/SS, R3.Pin_0
  N8: Part1.D12/MISO, Parking_2_-_Servo.pulse
  N9: Part1.D5_PWM, R4.Pin_0
  N10: Part1.D6_PWM, R5.Pin_0
  GND: Part1.GND, Parking_1_-_Servo.gnd, Parking_2_-_Servo.gnd, R2.Pin_1, R3.Pin_1, R4.Pin_1, R5.Pin_1
  VCC: Parking_1_-_Servo.vcc, Parking_2_-_Servo.vcc

notes:
  Serial communication between Raspberry Pi and Arduino
  LED1
  LED2
  Parking 1 - Section
  Parking 2 - Section
  POWER LED
